# Fritzing sketch fritzing_sketch (saved by Fritzing 1.0.3b)

parts:
  Part1 = Arduino Uno (Rev3)
  Part2 = Adafruit Proto Shield R3 [part_number="Adafruit #2077"]
  P1 = S1133 Si Photodiode [package="8mm Ceramic [THT]"]
  R1 = Resistor [tolerance=±5% power=0.25W resistance=1M package=THT]
  TLV1 = DIP - 8 pins [chip_label=TLV2462 package="DIP (Dual Inline) [THT]"]

nets:
  N1: Part1.A0, Part2.A0, Part2.1#163, Part2.P$5#164, Part2.P$6#165, R1.Pin_1, TLV1.OUT1
  5V: Part1.5V, Part2.+5V, Part2.P$5#161, Part2.P$6#162, TLV1.IN2+
  GND: Part1.GND, Part2.GND, Part2.1#117, Part2.P$5#118, Part2.P$6#119, Part2.1#120, Part2.P$5#121, Part2.P$6#122, Part2.N$146, P1.anode, TLV1.IN1+, TLV1.GND
  N2: Part2.1#0, Part2.P$5#1, Part2.1#126, Part2.P$5#127, Part2.P$6#128, Part2.1#180, Part2.P$6#182, P1.cathode, R1.Pin_0, TLV1.IN1-
  N3: Part2.D0, Part2.N$199
  N4: Part2.D1, Part2.N$198
  N5: Part2.D2, Part2.N$132
  N6: Part2.D3, Part2.N$128
  N7: Part2.D4, Part2.N$1
  N8: Part2.D5, Part2.N$171
  N9: Part2.D6, Part2.N$137
  N10: Part2.D7, Part2.N$136

custom parts:
  Adafruit Proto Shield R3: This prototyping shield is the best out there (well, we think so, at least), and now is even better with Version R3 - updated for the most compatibility with just about all the Arduinos! It works with UNO, Mega, Leonardo, NG, Diecimila, Duemilanove, and compatible Arduinos. Yun's and Arduino Ethernets have a chunky Ethernet jack that gets in the way of stacking, you can use the stacking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
  DIP - 8 pins: Dual OP Amp from Adafruit
